// Digital circuit hw3_c.dig as structural Verilog
module hw3_c (
  input  [3:0] X,
  input  [3:0] Y,
  output [3:0] Z
);

  wire comparator_1_lt;
  wire [3:0] add_1_s, add_2_s;

  Comparator #(.Bits(4)) comparator_1 (.a(X), .b(Y), .lt(comparator_1_lt));  // open: gt, eq
  Add #(.Bits(4)) add_1 (.a(X), .b(4'b0100), .c_i(1'b0), .s(add_1_s));  // open: c_o
  Add #(.Bits(4)) add_2 (.a(Y), .b(4'b0110), .c_i(1'b0), .s(add_2_s));  // open: c_o
  Multiplexer #(.Bits(4)) multiplexer_1 (.sel(comparator_1_lt), .in_0(add_2_s), .in_1(add_1_s), .out(Z));
endmodule
