// Digital circuit dds.dig as structural Verilog
module dds (
  input  [1:0] in_1,
  input  [1:0] in_2,
  input  clk,
  output [17:0] Amp_and_Interpolated
);

  wire and_1_out, and_2_out, and_3_out, and_4_out, and_5_out, and_6_out, and_7_out, cw0, cw1, cw2, cw3, cw4,
       dipswitch_1_out, dipswitch_2_out, dipswitch_3_out, dipswitch_4_out, dipswitch_5_out, not_1_out,
       not_2_out, or_1_out, Z_0_n, Z_1_n;
  wire [7:0] add_2_s, multiplexer_2_out;
  wire [15:0] add_1_s, add_3_s, Base_q, BRAM_d, multiplexer_1_out, Next_q, register_1_q, sub_1_s;
  wire [31:0] mul_1_mul;
  wire [33:0] mul_2_mul;

  Multiplexer #(.Selector_Bits(2), .Bits(16)) multiplexer_1 (
    .sel(in_1), .in_0(16'ha00), .in_1(16'hff00), .in_2(16'h55), .in_3(16'h1), .out(multiplexer_1_out));
  not not_1 (not_1_out, Z_1_n);
  not not_2 (not_2_out, Z_0_n);
  Add #(.Bits(16)) add_1 (.a(multiplexer_1_out), .b(register_1_q), .c_i(1'b0), .s(add_1_s));  // open: c_o
  and and_1 (and_1_out, Z_0_n, not_1_out);
  and and_2 (and_2_out, not_2_out, Z_1_n);
  and and_3 (and_3_out, not_2_out, not_1_out);
  and and_4 (and_4_out, not_2_out, Z_1_n);
  and and_5 (and_5_out, Z_0_n, not_1_out);
  and and_6 (and_6_out, not_2_out, Z_1_n);
  and and_7 (and_7_out, Z_0_n, Z_1_n);
  or or_1 (or_1_out, and_1_out, and_2_out);
  Register #(.Bits(16)) register_1 (.D(add_1_s), .C(clk), .en(cw0), .Q(register_1_q));
  or or_2 (cw0, and_3_out, dipswitch_1_out);
  DipSwitch dipswitch_1 (.out(dipswitch_1_out));
  or or_3 (cw1, and_4_out, dipswitch_2_out);
  DipSwitch dipswitch_2 (.out(dipswitch_2_out));
  or or_4 (cw2, and_5_out, dipswitch_3_out);
  DipSwitch dipswitch_3 (.out(dipswitch_3_out));
  or or_5 (cw3, and_6_out, dipswitch_4_out);
  DipSwitch dipswitch_4 (.out(dipswitch_4_out));
  or or_6 (cw4, and_7_out, dipswitch_5_out);
  DipSwitch dipswitch_5 (.out(dipswitch_5_out));
  // Probe on register_1_q
  D_FF u_Z_1_n (.D(or_1_out), .C(clk), .Q(Z_1_n));  // open: nQ
  D_FF #(.Default(1)) u_Z_0_n (.D(not_2_out), .C(clk), .Q(Z_0_n));  // open: nQ
  // Probe on register_1_q[7:0]
  // Probe on register_1_q[15:8]
  Add #(.Bits(8)) add_2 (.a(8'h1), .b(register_1_q[15:8]), .c_i(1'b0), .s(add_2_s));  // open: c_o
  // Probe on add_2_s
  // Probe on multiplexer_2_out
  Multiplexer #(.Bits(8)) multiplexer_2 (.sel(cw1), .in_0(register_1_q[15:8]), .in_1(add_2_s), .out(multiplexer_2_out));
  ROM #(.AddrBits(8), .Bits(16)) BRAM (.A(multiplexer_2_out), .sel(1'b1), .D(BRAM_d));
  // ScopeTrigger #(.trigger("rising")) scopetrigger_1: pin names not known; wires that end beside it: cw4
  Register #(.Bits(16)) Base (.D(BRAM_d), .C(clk), .en(cw2), .Q(Base_q));
  Register #(.Bits(16)) Next (.D(BRAM_d), .C(clk), .en(cw3), .Q(Next_q));
  // Probe on Base_q
  // Probe on Next_q
  Sub #(.Bits(16)) sub_1 (.a(Next_q), .b(Base_q), .c_i(1'b0), .s(sub_1_s));  // open: c_o
  Mul #(.Signed("true"), .Bits(16)) mul_1 (.a({{8{1'b0}}, register_1_q[7:0]}), .b(sub_1_s), .mul(mul_1_mul));
  Add #(.Bits(16)) add_3 (.a(mul_1_mul[23:8]), .b(Base_q), .c_i(1'b0), .s(add_3_s));  // open: c_o
  Mul #(.Signed("true"), .Bits(17)) mul_2 (.a({1'b0, add_3_s}), .b({{15{1'b0}}, in_2}), .mul(mul_2_mul));
  Register #(.Bits(18)) register_2 (.D(mul_2_mul[17:0]), .C(clk), .en(cw4), .Q(Amp_and_Interpolated));

  // Notes on the sheet:
  //   in_2: default 1
  //   clk: Hz: 20
  //   Lab4 dp
  //   Lab4 cu
  //   IndexOffsetReg
  //   Phase Inc
  //   Offset
  //   Index
  //   LookupTable
  //   BaseAndNextReg
  //   Interpolate
  //   Base
  //   Next
  //   Pad MSB
  //   Truncate
  //   Delta*Offset
  //   Amplify by
  //   Amplify
  //   Base+Delta*Offset
  //   Amp*(Base+Delta*Offset)
  //   ResultReg
endmodule
